# Fritzing sketch otamatone_breakout (saved by Fritzing 0.9.3b)
circuit board: 8.46667cm x 5.64444cm

parts:
  C2 = Ceramic Capacitor [capacitance=100nF package="0603 [SMD, multilayer]"]
  J2 = male pin header, 3 pins [form="♂ (male)"]
  Neck = male pin header, 2 pins [form="♂ (male)"]
  Line_In = male pin header, 3 pins [form="♂ (male)"]
  R9 = Resistor [tolerance=±5% resistance=2.2k package="0603 [SMD]"]
  R4 = Resistor [tolerance=±5% resistance=10k package="0603 [SMD]"]
  C7 = Tantalum Capacitor [capacitance=10µF package="B 3528 [SMD, tantalum]"]
  Buttons = male pin header, 3 pins [form="♂ (male)"]
  Switch = male pin header, 3 pins [form="♂ (male)"]
  Volume = male pin header, 3 pins [form="♂ (male)"]
  R13 = Resistor [tolerance=±5% resistance=47k package="0603 [SMD]"]
  C5 = Tantalum Capacitor [capacitance=10µF package="B 3528 [SMD, tantalum]"]
  C6 = Tantalum Capacitor [capacitance=10µF package="B 3528 [SMD, tantalum]"]
  Line_Out = male pin header, 2 pins [form="♂ (male)"]
  OLED = male pin header, 4 pins [form="♂ (male)"]
  C4 = Ceramic Capacitor [capacitance=100nF package="0805 [SMD, multilayer]"]
  C3 = Ceramic Capacitor [capacitance=100nF package="0805 [SMD, multilayer]"]
  R12 = Resistor [tolerance=±5% resistance=47k package="0805 [SMD]"]
  R6 = Resistor [tolerance=±5% resistance=47k package="0805 [SMD]"]
  R3 = Resistor [tolerance=±5% resistance=62k package="0805 [SMD]"]
  R2 = Resistor [tolerance=±5% resistance=10k package="0805 [SMD]"]
  J1 = male pin header, 14 pins [form="♂ (male)"]
  R1 = Resistor [tolerance=±5% resistance=10k package="0805 [SMD]"]
  R5 = Resistor [tolerance=±5% resistance=10k package="0805 [SMD]"]
  R8 = Resistor [tolerance=±5% resistance=47k package="0805 [SMD]"]
  R7 = Resistor [tolerance=±5% resistance=10k package="0805 [SMD]"]

nets:
  DAC: C2.0, J2.pin3
  N1: C2.1, Line_Out.pin1
  DGND: J2.pin1, R4.Pin_1, OLED.pin3, R5.Pin_1
  PRGM: J2.pin2
  3v3: Neck.pin1, Buttons.pin3, Volume.pin1, R2.Pin_1, J1.pin3, R1.Pin_1, R7.Pin_0
  NECK: Neck.pin2, C3.1, R3.Pin_0, J1.pin7
  N2: Line_In.pin1, C5.-, R8.Pin_0
  N3: Line_In.pin2, C7.-, R13.Pin_0
  AGND: Line_In.pin3, R9.Pin_1, Volume.pin3, R13.Pin_1, C6.-, Line_Out.pin2, C4.1, C3.0, R3.Pin_1, J1.pin2, R8.Pin_1
  N4: R9.Pin_0, C6.+, R12.Pin_1, R6.Pin_1, R7.Pin_1
  BT1: R4.Pin_0, Buttons.pin1, J1.pin6
  INR: C7.+, R12.Pin_0, J1.pin10
  BT0: Buttons.pin2, J1.pin5, R5.Pin_0
  Vin: Switch.pin1, Switch.pin2
  5v0: Switch.pin3, OLED.pin4, J1.pin1
  VPOT: Volume.pin2, C4.0, J1.pin4
  INL: C5.+, R6.Pin_0, J1.pin11
  SDA: OLED.pin1, R2.Pin_0, J1.pin9
  SCL: OLED.pin2, J1.pin8, R1.Pin_0
  A12: J1.pin12
  A14: J1.pin13
  A13: J1.pin14
